# Fritzing sketch wiringDiagramFritzing (saved by Fritzing 0.9.3b)
breadboards: 1

parts:
  Raspberry_Pi_1 = Raspberry Pi 3 [part_number=RPI-3-V1.2]
  DS2 = DS18B20 1-Wire Temperature Sensor [part_number=DS18B20]
  R1 = Resistor [tolerance=±5% resistance=4.7k package="0402 [SMD]"]

nets:
  GND: Raspberry_Pi_1.GND, DS2.GND
  N1: Raspberry_Pi_1.GPIO17, DS2.DQ, R1.Pin_1
  3V3: Raspberry_Pi_1.3V3, DS2.VDD, R1.Pin_0
